# Fritzing sketch pedal (saved by Fritzing 0.9.1b)
breadboards: 1

parts:
  Part1 = Arduino Micro (Rev3)
  R1 = Resistor [tolerance=±5% resistance=220 package=THT]
  R2 = Resistor [tolerance=±5% resistance=220 package=THT]
  DIN1 = DIN-5 jack (MIDI) [package=THT]
  D1 = Rectifier Diode [part_number=1N914 package="300 mil [THT]"]
  R3 = Resistor [tolerance=±5% resistance=1k package=THT]
  S1 = Pushbutton [package=THT]
  S2 = Pushbutton [package=THT]
  S3 = Pushbutton [package=THT]
  S4 = Pushbutton [package=THT]
  S7 = Pushbutton [package=THT]
  S8 = Pushbutton [package=THT]
  S5 = Pushbutton [package=THT]
  S6 = Pushbutton [package=THT]
  S10 = Pushbutton [package=THT]
  S12 = Pushbutton [package=THT]
  S9 = Pushbutton [package=THT]
  S11 = Pushbutton [package=THT]
  S14 = Pushbutton [package=THT]
  S15 = Pushbutton [package=THT]
  S13 = Pushbutton [package=THT]
  S16 = Pushbutton [package=THT]
  D2 = Rectifier Diode [part_number=1N914 package="300 mil [THT]"]
  R4 = Resistor [tolerance=±5% resistance=1k package=THT]
  D3 = Rectifier Diode [part_number=1N914 package="300 mil [THT]"]
  R5 = Resistor [tolerance=±5% resistance=1k package=THT]
  D4 = Rectifier Diode [part_number=1N914 package="300 mil [THT]"]
  R6 = Resistor [tolerance=±5% resistance=1k package=THT]
  VBAT1 = Battery
  VBAT2 = Battery

nets:
  N1: Part1.D1/TX, R2.Pin_1
  N2: Part1.D2/SDA, R3.Pin_0
  N3: Part1.D3/SCL, R4.Pin_0
  N4: Part1.D4_PWM/A6, R5.Pin_0
  N5: Part1.D5_PWM, R6.Pin_0
  N6: Part1.D6_PWM/A7, S1.leg1, S2.leg1, S3.leg1, S4.leg1
  N7: Part1.D7, S7.leg1, S8.leg1, S5.leg1, S6.leg1
  N8: Part1.D8_PWM/A8, S10.leg1, S12.leg1, S9.leg1, S11.leg1
  N9: Part1.D9_PWM/A9, S14.leg1, S15.leg1, S13.leg1, S16.leg1
  N10: R1.Pin_0, DIN1.4
  N11: R2.Pin_0, DIN1.5
  N12: D1.cathode, R3.Pin_1
  N13: D1.anode, S1.leg0, S5.leg0, S9.leg0, S13.leg0
  N14: S2.leg0, S6.leg0, S10.leg0, S14.leg0, D2.anode
  N15: S3.leg0, S7.leg0, S11.leg0, S15.leg0, D3.anode
  N16: S4.leg0, S8.leg0, S12.leg0, S16.leg0, D4.anode
  N17: D2.cathode, R4.Pin_1
  N18: D3.cathode, R5.Pin_1
  N19: D4.cathode, R6.Pin_1
  N20: VBAT1.-, VBAT2.+
